# Fritzing sketch Radar (saved by Fritzing 0.9.3b)
breadboards: 1

parts:
  J1 = Basic Servo
  hc-sr1 = hc-sr04
  LED1 = smd LED [color="Green (570nm)" package="0805 [SMD]"]
  Part1 = Arduino Uno (Rev3) - ICSP
  R1 = Resistor [tolerance=±5% resistance=220 package=THT]
  Raspberry_Pi1 = Raspberry Pi 2  # not connected

nets:
  GND: J1.gnd, hc-sr1.GND, Part1.GND, R1.Pin_1
  VCC: J1.vcc, hc-sr1.VCC, Part1.5V
  N1: J1.pulse, Part1.ICSP_MISO, Part1.D12/MISO
  N2: hc-sr1.Trig, Part1.D10_PWM/SS
  N3: hc-sr1.Echo, Part1.D11_PWM/MOSI
  N4: LED1.cathode, R1.Pin_0
  N5: LED1.anode, Part1.D13/SCK
